// Logisim project hw4.circ as structural Verilog
module register (
  input  [15:0] rIn,
  input  Reset,
  input  clock,
  input  wEnable,
  output [15:0] rOut
);

  wire [15:0] and_1_out, multiplexer_1_out, multiplexer_2_out;

  D_Flip_Flop d_ff_1 (.clk(clock), .D(multiplexer_2_out[15]), .Q(rOut[15]));  // open: Qn, preset, en, reset
  D_Flip_Flop d_ff_2 (.clk(clock), .D(multiplexer_2_out[14]), .Q(rOut[14]));  // open: Qn, preset, en, reset
  D_Flip_Flop d_ff_3 (.clk(clock), .D(multiplexer_2_out[13]), .Q(rOut[13]));  // open: Qn, preset, en, reset
  D_Flip_Flop d_ff_4 (.clk(clock), .D(multiplexer_2_out[12]), .Q(rOut[12]));  // open: Qn, preset, en, reset
  assign and_1_out = rIn & {16{1'b0}};  // AND_Gate and_1, 16 bits wide
  D_Flip_Flop d_ff_5 (.clk(clock), .D(multiplexer_2_out[11]), .Q(rOut[11]));  // open: Qn, preset, en, reset
  Multiplexer #(.width(16), .enable("false")) multiplexer_1 (
    .in0(rIn), .in1(and_1_out), .out(multiplexer_1_out), .sel(Reset));
  D_Flip_Flop d_ff_6 (.clk(clock), .D(multiplexer_2_out[10]), .Q(rOut[10]));  // open: Qn, preset, en, reset
  D_Flip_Flop d_ff_7 (.clk(clock), .D(multiplexer_2_out[9]), .Q(rOut[9]));  // open: Qn, preset, en, reset
  Multiplexer #(.width(16), .enable("false")) multiplexer_2 (
    .in0(rOut), .in1(multiplexer_1_out), .out(multiplexer_2_out), .sel(wEnable));
  D_Flip_Flop d_ff_8 (.clk(clock), .D(multiplexer_2_out[8]), .Q(rOut[8]));  // open: Qn, preset, en, reset
  D_Flip_Flop d_ff_9 (.clk(clock), .D(multiplexer_2_out[7]), .Q(rOut[7]));  // open: Qn, preset, en, reset
  D_Flip_Flop d_ff_10 (.clk(clock), .D(multiplexer_2_out[6]), .Q(rOut[6]));  // open: Qn, preset, en, reset
  D_Flip_Flop d_ff_11 (.clk(clock), .D(multiplexer_2_out[5]), .Q(rOut[5]));  // open: Qn, preset, en, reset
  D_Flip_Flop d_ff_12 (.clk(clock), .D(multiplexer_2_out[4]), .Q(rOut[4]));  // open: Qn, preset, en, reset
  D_Flip_Flop d_ff_13 (.clk(clock), .D(multiplexer_2_out[3]), .Q(rOut[3]));  // open: Qn, preset, en, reset
  D_Flip_Flop d_ff_14 (.clk(clock), .D(multiplexer_2_out[2]), .Q(rOut[2]));  // open: Qn, preset, en, reset
  D_Flip_Flop d_ff_15 (.clk(clock), .D(multiplexer_2_out[1]), .Q(rOut[1]));  // open: Qn, preset, en, reset
  D_Flip_Flop d_ff_16 (.clk(clock), .D(multiplexer_2_out[0]), .Q(rOut[0]));  // open: Qn, preset, en, reset

  // Other names for the same wires on the sheet: clk = clock; ot[15:0] = rOut
endmodule

module rfile (
  input  reset,
  input  clk,
  input  [15:0] WriteData,
  input  [2:0] ReadReg1,
  input  [2:0] ReadReg2,
  input  [2:0] rd,
  input  [2:0] WriteReg,
  output [15:0] ReadData1,
  output [15:0] ReadData2
);

  wire and_1_out, decoder_2_out0, decoder_2_out1, decoder_2_out2, decoder_2_out3, decoder_2_out4,
       decoder_2_out5, decoder_2_out6, decoder_2_out7, decoder_3_out0, decoder_3_out1, decoder_3_out2,
       decoder_3_out3, decoder_3_out4, decoder_3_out5, decoder_3_out6, decoder_3_out7, w0, w1, w2, w3, w4,
       w5, w6, w7;
  wire [15:0] five, four, one, sev, six, three, two, zero;

  assign ReadData2 = decoder_2_out0 ? zero : 16'bz;  // Controlled_Buffer controlled_buffer_1
  assign ReadData2 = decoder_2_out2 ? two : 16'bz;  // Controlled_Buffer controlled_buffer_2
  assign ReadData2 = decoder_2_out1 ? one : 16'bz;  // Controlled_Buffer controlled_buffer_3
  Decoder #(.select(3)) decoder_1 (
    .out0(w0), .out1(w1), .out2(w2), .out3(w3), .out4(w4), .out5(w5), .out6(w6), .out7(w7), .sel(WriteReg),
    .en(1'b1));
  assign ReadData2 = decoder_2_out5 ? two : 16'bz;  // Controlled_Buffer controlled_buffer_4
  assign ReadData2 = decoder_2_out4 ? one : 16'bz;  // Controlled_Buffer controlled_buffer_5
  assign ReadData2 = decoder_2_out3 ? zero : 16'bz;  // Controlled_Buffer controlled_buffer_6
  Decoder #(.select(3)) decoder_2 (
    .out0(decoder_2_out0), .out1(decoder_2_out1), .out2(decoder_2_out2), .out3(decoder_2_out3),
    .out4(decoder_2_out4), .out5(decoder_2_out5), .out6(decoder_2_out6), .out7(decoder_2_out7),
    .sel(ReadReg2), .en(1'b1));
  assign ReadData2 = decoder_2_out7 ? two : 16'bz;  // Controlled_Buffer controlled_buffer_7
  assign ReadData2 = decoder_2_out6 ? one : 16'bz;  // Controlled_Buffer controlled_buffer_8
  register r0 (.rIn({16{1'b0}}), .clock(clk), .Reset(reset), .wEnable(and_1_out), .rOut(zero));
  and and_1 (and_1_out, 1'b0, w0);
  register r1 (.rIn(WriteData), .clock(clk), .Reset(reset), .wEnable(w1), .rOut(one));
  // Probe on one
  register r2 (.rIn(WriteData), .clock(clk), .Reset(reset), .wEnable(w2), .rOut(two));
  register r3 (.rIn(WriteData), .clock(clk), .Reset(reset), .wEnable(w3), .rOut(three));
  register r4 (.rIn(WriteData), .clock(clk), .Reset(reset), .wEnable(w4), .rOut(four));
  register r5 (.rIn(WriteData), .clock(clk), .Reset(reset), .wEnable(w5), .rOut(five));
  assign ReadData1 = decoder_3_out2 ? two : 16'bz;  // Controlled_Buffer controlled_buffer_9
  assign ReadData1 = decoder_3_out1 ? one : 16'bz;  // Controlled_Buffer controlled_buffer_10
  assign ReadData1 = decoder_3_out0 ? zero : 16'bz;  // Controlled_Buffer controlled_buffer_11
  register r6 (.rIn(WriteData), .clock(clk), .Reset(reset), .wEnable(w6), .rOut(six));
  assign ReadData1 = decoder_3_out5 ? five : 16'bz;  // Controlled_Buffer controlled_buffer_12
  assign ReadData1 = decoder_3_out4 ? four : 16'bz;  // Controlled_Buffer controlled_buffer_13
  assign ReadData1 = decoder_3_out3 ? three : 16'bz;  // Controlled_Buffer controlled_buffer_14
  Decoder #(.select(3)) decoder_3 (
    .out0(decoder_3_out0), .out1(decoder_3_out1), .out2(decoder_3_out2), .out3(decoder_3_out3),
    .out4(decoder_3_out4), .out5(decoder_3_out5), .out6(decoder_3_out6), .out7(decoder_3_out7),
    .sel(ReadReg1), .en(1'b1));
  assign ReadData1 = decoder_3_out7 ? sev : 16'bz;  // Controlled_Buffer controlled_buffer_15
  assign ReadData1 = decoder_3_out6 ? six : 16'bz;  // Controlled_Buffer controlled_buffer_16
  register r7 (.rIn(WriteData), .clock(clk), .Reset(reset), .wEnable(w7), .rOut(sev));

  // Other names for the same wires on the sheet: clkT = clk; reg1Num[2:0] = ReadReg1; reg2Num[2:0] = ReadReg2;
  //   wvalT[15:0] = WriteData
endmodule

module add (
  input  cin,
  input  a,
  input  b,
  output sum,
  output carry
);

  wire and_1_out, and_2_out, xor_1_out;

  xor xor_1 (xor_1_out, a, b);
  and and_1 (and_1_out, b, a);
  and and_2 (and_2_out, cin, xor_1_out);
  xor xor_2 (sum, cin, xor_1_out);
  or or_1 (carry, and_2_out, and_1_out);

  // Notes on the sheet:
  //   carry
endmodule

module adder (
  input  [15:0] A,
  input  [15:0] B,
  output ovf,
  output [15:0] result
);

  wire add_2_carry, add_3_carry, add_4_carry, add_5_carry, add_6_carry, add_7_carry, add_8_carry,
       add_9_carry, add_10_carry, add_11_carry, add_12_carry, add_13_carry, add_14_carry, add_15_carry,
       add_16_carry;

  add add_1 (.cin(add_2_carry), .a(A[15]), .b(B[15]), .sum(result[15]), .carry(ovf));
  add add_2 (.cin(add_3_carry), .a(A[14]), .b(B[14]), .sum(result[14]), .carry(add_2_carry));
  add add_3 (.cin(add_4_carry), .a(A[13]), .b(B[13]), .sum(result[13]), .carry(add_3_carry));
  add add_4 (.cin(add_5_carry), .a(A[12]), .b(B[12]), .sum(result[12]), .carry(add_4_carry));
  add add_5 (.cin(add_6_carry), .a(A[11]), .b(B[11]), .sum(result[11]), .carry(add_5_carry));
  add add_6 (.cin(add_7_carry), .a(A[10]), .b(B[10]), .sum(result[10]), .carry(add_6_carry));
  add add_7 (.cin(add_8_carry), .a(A[9]), .b(B[9]), .sum(result[9]), .carry(add_7_carry));
  add add_8 (.cin(add_9_carry), .a(A[8]), .b(B[8]), .sum(result[8]), .carry(add_8_carry));
  add add_9 (.cin(add_10_carry), .a(A[7]), .b(B[7]), .sum(result[7]), .carry(add_9_carry));
  add add_10 (.cin(add_11_carry), .a(A[6]), .b(B[6]), .sum(result[6]), .carry(add_10_carry));
  add add_11 (.cin(add_12_carry), .a(A[5]), .b(B[5]), .sum(result[5]), .carry(add_11_carry));
  add add_12 (.cin(add_13_carry), .a(A[4]), .b(B[4]), .sum(result[4]), .carry(add_12_carry));
  add add_13 (.cin(add_14_carry), .a(A[3]), .b(B[3]), .sum(result[3]), .carry(add_13_carry));
  add add_14 (.cin(add_15_carry), .a(A[2]), .b(B[2]), .sum(result[2]), .carry(add_14_carry));
  add add_15 (.cin(add_16_carry), .a(A[1]), .b(B[1]), .sum(result[1]), .carry(add_15_carry));
  add add_16 (.cin(1'b0), .a(A[0]), .b(B[0]), .sum(result[0]), .carry(add_16_carry));
endmodule
